# Fritzing sketch arduino_dallas_bme280_mosfet (saved by Fritzing 0.9.4)
breadboards: 1

parts:
  元件1 = Arduino Nano (Rev3.0)
  DS1 = DS18B20 1-Wire Temperature Sensor [part_number=DS18B20]
  DS2 = DS18B20 1-Wire Temperature Sensor [part_number=DS18B20]
  DS3 = DS18B20 1-Wire Temperature Sensor [part_number=DS18B20]
  元件2 = BME280 Breakout  # not connected
  LED1 = smd LED [color="Red (633nm)" package="0805 [SMD]"]
  元件3 = IFR520 MOS module [package=THT]
  R1 = Resistor [tolerance=±5% resistance=330 package=THT]
  R2 = Resistor [tolerance=±1% resistance=4.7k package=THT]

nets:
  GND: 元件1.GND, DS1.GND, DS2.GND, DS3.GND, 元件3.GND
  N1: 元件1.D2, DS1.DQ, DS2.DQ, DS3.DQ, R2.Pin_0
  N2: 元件1.D6, 元件3.SIG
  VDD: 元件1.5V, DS1.VDD, DS2.VDD, DS3.VDD, 元件3.VCC, R2.Pin_1
  N3: LED1.cathode, 元件3.V-
  N4: LED1.anode, R1.Pin_0
  N5: 元件3.V+, R1.Pin_1
