# Fritzing sketch arduino_desk (saved by Fritzing 0.9.4)
breadboards: 1

parts:
  Mod1 = Arduino MKR Wifi 1010
  Mod2 = KY-015 Temperature & Humidity Sensor Module [package="Breakout board"]
  S3 = Momentary Switch [package=ksa_sealed_tac_switch]
  S4 = Momentary Switch [package=ksa_sealed_tac_switch]
  R1 = Rotary Potentiometer (Small) [maximum_resistance=100kΩ package=THT]
  元件1 = HC-SR501 Body Sensor Module
  Grove1 = Grove OLED 128x96

nets:
  N1: Mod1.A2, R1.wiper
  N2: Mod1.~D4, 元件1.OUT
  N3: Mod1.~D5, S3.2
  N4: Mod1.D6, S4.2
  N5: Mod1.D7, Mod2.S
  N6: Mod1.D11/SDA, Grove1.SDA
  N7: Mod1.D12/SCL, Grove1.SCL
  VCC: Mod2.Vin, R1.leg2, 元件1.VCC, Grove1.VCC
  GND: Mod2.-, S3.4, S4.4, R1.leg1, 元件1.GND, Grove1.GND

custom parts:
  Arduino MKR Wifi 1010: Arduino MKR Wifi 1010, SAMD21 Cortex-M0+ 32bit Low Power ARM MCU,Flash Memory 256 KB, SRAM 32KB, 48mhz clock, Ublok Wifi interface.
  KY-015 Temperature & Humidity Sensor Module: KY-015 temperature and humidity sensor module, provides a low-latency serial interface to measure humidity and temperature.
  HC-SR501 Body Sensor Module: Pyroelectric Infrared PIR Motion Sensor Detector Module
